# Fritzing sketch schematic (saved by Fritzing 0.9.9b)
breadboards: 1

parts:
  U1 = Photon
  K1 = songle relay [part_number=SRD-5VDC-SL-C]
  R1 = Resistor [tolerance=±5% power=100W resistance=1.5 part_number="Cartridge Heater" package=THT]
  DS1 = DS18B20 1-Wire Temperature Sensor [part_number=DS18B20]
  R2 = Resistor [tolerance=±5% power=0.25 resistance=4.7k package=THT]

nets:
  GND: U1.GND, K1.COMMON, K1.GND, DS1.GND
  N1: U1.D0, DS1.DQ, R2.Pin_1
  3V3: U1.3V3, DS1.VDD, R2.Pin_0
  12V: K1.VCC, R1.Pin_0
  N2: K1.NO, R1.Pin_1
